# Fritzing sketch grbl_board (saved by Fritzing 0.9.3b)
circuit board: 8.43767cm x 7.42783cm
breadboards: 1

parts:
  U1 = atmega328 [package=dip]
  R1 = Resistor [tolerance=±5% resistance=220 package=THT]
  C2 = Ceramic Capacitor [capacitance=22pF package="100 mil [THT, multilayer]"]
  C3 = Ceramic Capacitor [capacitance=22pF package="100 mil [THT, multilayer]"]
  XTAL1 = Crystal [frequency="16 Mhz" package=THT]
  J_MOTORS = male pin header, 12 pins [form="♂ (male)"]
  J_PROGRAMMER = AVR ISP 6 Pin [package=2x3_lock]
  J_ZLIMIT = double row male pin header, 2 pins [form="♂ (male)"]
  J_XLIMIT = double row male pin header, 2 pins [form="♂ (male)"]
  J_YLIMIT = double row male pin header, 2 pins [form="♂ (male)"]
  J_COOLANT = double row male pin header, 2 pins [form="♂ (male)"]
  J_PROBE = double row male pin header, 2 pins [form="♂ (male)"]
  J_RS232 = female pin header, 5 pins [form="♀ (female)"]
  J_RESUME = double row male pin header, 2 pins [form="♂ (male)"]
  J_FEEDHOLD = double row male pin header, 2 pins [form="♂ (male)"]
  J_ABORT = double row male pin header, 2 pins [form="♂ (male)"]
  D1 = Rectifier Diode [part_number=1N4001 package="300 mil [THT]"]
  D2 = Rectifier Diode [part_number=1N4001 package="300 mil [THT]"]

nets:
  RESET: U1.RESET, R1.Pin_1, J_PROGRAMMER.5
  RS232_TX: U1.D0_(RX), J_RS232.pin3
  RS232_RX: U1.D1_(TX), J_RS232.pin2
  STEPX: U1.D2, J_MOTORS.pin5
  STEPY: U1.D3_(PWM), J_MOTORS.pin6
  STEPZ: U1.D4, J_MOTORS.pin7
  5V: U1.VCC, U1.AVCC, U1.AREF, R1.Pin_0, J_PROGRAMMER.2, J_RS232.pin5
  GND: U1.GND, C2.0, C3.0, J_MOTORS.pin12, J_PROGRAMMER.6, J_ZLIMIT.pin2, J_XLIMIT.pin2, J_YLIMIT.pin2, J_COOLANT.pin2, J_PROBE.pin2, J_RS232.pin4, J_RESUME.pin2, J_FEEDHOLD.pin2, J_ABORT.pin2, D1.anode, D2.anode
  N1: U1.XLAT1, C3.1, XTAL1.pin_0
  N2: U1.XLAT2, C2.1, XTAL1.pin_1
  DIRX: U1.D5_(PWM), J_MOTORS.pin8
  DIRY: U1.D6_(PWM), J_MOTORS.pin9
  DIRZ: U1.D7, J_MOTORS.pin10
  STEPPERENABLE: U1.D8, J_MOTORS.pin2
  XLIMIT: U1.D9_(PWM), J_XLIMIT.pin1
  YLIMIT: U1.D10_(PWM), J_YLIMIT.pin1
  SPINDLEPWM: U1.D11_(PWM), J_MOTORS.pin3, J_PROGRAMMER.4
  ZLIMIT: U1.D12, J_PROGRAMMER.1, J_ZLIMIT.pin1
  SPINDLEDIRECTION: U1.D13, J_MOTORS.pin4, J_PROGRAMMER.3, D2.cathode
  ABORT: U1.A0, J_ABORT.pin1
  FEEDHOLD: U1.A1, J_FEEDHOLD.pin1
  RESUME: U1.A2, J_RESUME.pin1
  COOLANT: U1.A3, J_COOLANT.pin1, D1.cathode
  PROBE: U1.A5, J_PROBE.pin1
  RS232_RST: J_RS232.pin1
